// Logisim project 8bit_accumulator_CPU.circ as structural Verilog: 33 circuits, main circuit main
module main (
  input  [7:0] DATA_IN,
  input  in_2,
  input  on_off,
  output [7:0] DATA_OUT,
  output [7:0] out_5,
  output [7:0] out_6,
  output [7:0] out_7,
  output [7:0] out_8,
  output [7:0] out_9,
  output [7:0] out_10,
  output [7:0] out_11,
  output [7:0] out_12,
  output [7:0] out_13,
  output [7:0] out_14,
  output [7:0] out_15,
  output [7:0] out_16,
  output [7:0] out_17,
  output [7:0] out_18,
  output [7:0] out_19,
  output [7:0] out_20
);

  wire a0_t, a1_t, a2_t, a3_t, a4, a5, a6, a7, a8, a9, a10, a11, a12, a13, a14, a15, a16, a17, a18, a19, a20,
       a32, a33, a34, a35, a36, a37, a38, accumulatore_1_or_ac, and_1_out, boot_controller_1_a_boot, C,
       or_1_out, or_2_out, or_3_out, r_fun_t1_1_or_t1, r_fun_t2_1_or_t2, reset, rst_addr, S_ext;
  wire [1:0] A0, A1;
  wire [2:0] A2;
  wire [3:0] A3, alu_1_flags, demultiplexer_1_out0, demultiplexer_1_out1, demultiplexer_1_out2,
       demultiplexer_2_out0, ind, ir_1_cop, ir_1_ind, multiplexer_1_out, pc_1_y;
  wire [7:0] accumulatore_1_y, alu_1_ris, demultiplexer_2_out1, demultiplexer_2_out2, demultiplexer_2_out3,
       demultiplexer_2_out4, demultiplexer_2_out5, demultiplexer_2_out6, demultiplexer_2_out7,
       demultiplexer_2_out8, ext_1_y, multiplexer_2_out, r_fun_t1_1_y, r_fun_t2_1_y, r_ms_8bit_z_1_y,
       ram_16byte_1_out_mbr, registro_ms_8bit_1_y, rom_1_data;
  wire [7:4] demultiplexer_2_out0_2;

  boot_controller boot_controller_1 (.C(C), .start(in_2), .A_boot(boot_controller_1_a_boot), .S_ram(S_ext));
  boot_counter boot_counter_1 (.rst_addr(rst_addr), .A(boot_controller_1_a_boot), .C(C), .y(ind));
  not not_1 (rst_addr, in_2);
  ROM #(.addrWidth(4)) rom_1 (.addr(ind), .data(rom_1_data));
  EXT ext_1 (.x(demultiplexer_1_out0), .k(a9), .y(ext_1_y));
  Clock clock_1 (.out(C));
  RAM_16byte ram_16byte_1 (
    .in_mbr(demultiplexer_2_out1), .in_mbr_ext(rom_1_data), .S(a7), .S_ext(S_ext), .ext(reset),
    .in_mar(demultiplexer_1_out1), .in_mar_ext(ind), .A_mar(a5), .A_mar_ext(reset), .C(and_1_out), .C_ext(C),
    .inc_mar(a32), .L(a8), .A_mbr(a6), .A_mbr_ext(reset), .l_12(out_17), .l_13(out_18), .l_14(out_19),
    .l_15(out_20), .out_mbr(ram_16byte_1_out_mbr), .l_0(out_5), .l_1(out_6), .l_2(out_7), .l_3(out_8),
    .l_4(out_9), .l_5(out_10), .l_6(out_11), .l_7(out_12), .l_8(out_13), .l_9(out_14), .l_10(out_15),
    .l_11(out_16));
  and and_1 (and_1_out, C, ~a36, on_off);  // AND_Gate
  not not_2 (reset, on_off);
  IR ir_1 (.A(or_1_out), .C(C), .x(demultiplexer_2_out3), .z(or_2_out), .cop(ir_1_cop), .ind(ir_1_ind));
  or or_1 (or_1_out, a0_t, reset);
  Accumulatore accumulatore_1 (
    .A(a4), .C(and_1_out), .x(demultiplexer_2_out4), .y(accumulatore_1_y), .or_AC(accumulatore_1_or_ac));
  or or_2 (or_2_out, a1_t, reset);
  Parte_Controllo_ROM parte_controllo_rom_1 (
    .b_ACC(accumulatore_1_or_ac), .b_T1(r_fun_t1_1_or_t1), .b_T2(r_fun_t2_1_or_t2), .istruzione(ir_1_cop),
    .reset(reset), .in_6(and_1_out),
    .s_alpha({a38, a37, a36, a35, a34, a33, a32, A3[0], A3[1], A3[2], A3[3], A2[0], A2[1], A2[2], A1[0], A1[1], A0[0], A0[1], a20, a19, a18, a17, a16, a15, a14, a13, a12, a11, a10, a9, a8, a7, a6, a5, a4, a3_t, a2_t, a1_t, a0_t}));
  Demultiplexer #(.select(2), .width(4)) demultiplexer_1 (
    .out0(demultiplexer_1_out0), .out1(demultiplexer_1_out1), .out2(demultiplexer_1_out2),
    .in(multiplexer_1_out), .sel(A1));  // open: out3
  Multiplexer #(.enable("true"), .select(2), .width(4)) multiplexer_1 (
    .in0(demultiplexer_2_out0), .in1(ir_1_ind), .in2(pc_1_y), .out(multiplexer_1_out), .sel(A0), .en(a34));  // open: in3
  Registro_MS_8bit registro_ms_8bit_1 (.A(a10), .C(and_1_out), .x(demultiplexer_2_out5), .y(registro_ms_8bit_1_y));
  Registro_MS_8bit registro_ms_8bit_2 (.A(a37), .C(and_1_out), .x(demultiplexer_2_out2), .y(DATA_OUT));
  PC pc_1 (.k0(a3_t), .k1(reset), .A(or_3_out), .C(C), .x(demultiplexer_1_out2), .y(pc_1_y));
  or or_3 (or_3_out, a2_t, reset);
  Demultiplexer #(.select(4), .width(8)) demultiplexer_2 (
    .out0({demultiplexer_2_out0_2, demultiplexer_2_out0}), .out1(demultiplexer_2_out1),
    .out2(demultiplexer_2_out2), .out3(demultiplexer_2_out3), .out4(demultiplexer_2_out4),
    .out5(demultiplexer_2_out5), .out6(demultiplexer_2_out6), .out7(demultiplexer_2_out7),
    .out8(demultiplexer_2_out8), .in(multiplexer_2_out), .sel(A3));  // open: out9, out10, out11, out12, out13, out14, out15
  Multiplexer #(.enable("true"), .select(3), .width(8)) multiplexer_2 (
    .in0(ext_1_y), .in1(ram_16byte_1_out_mbr), .in2(DATA_IN), .in3(accumulatore_1_y), .in4(alu_1_ris),
    .in5(r_fun_t1_1_y), .in6(r_fun_t2_1_y), .in7({4'b0000, alu_1_flags}), .out(multiplexer_2_out), .sel(A2),
    .en(a35));
  ALU alu_1 (
    .x1(a12), .x0(a14), .r_in(a13), .B(r_ms_8bit_z_1_y), .C(a38), .A(registro_ms_8bit_1_y),
    .flags(alu_1_flags), .ris(alu_1_ris));
  R_MS_8bit_Z r_ms_8bit_z_1 (.x(demultiplexer_2_out6), .Z(a33), .A(a11), .C(and_1_out), .y(r_ms_8bit_z_1_y));
  R_fun_T1 r_fun_t1_1 (
    .A(a15), .C(and_1_out), .T1_1(a16), .T1_0(a17), .x(demultiplexer_2_out7), .y(r_fun_t1_1_y),
    .OR_T1(r_fun_t1_1_or_t1));
  R_fun_T2 r_fun_t2_1 (
    .A(a18), .C(and_1_out), .T1_1(a19), .T1_0(a20), .x(demultiplexer_2_out8), .y(r_fun_t2_1_y),
    .OR_T2(r_fun_t2_1_or_t2));
endmodule

module FF_FC (
  input  F,
  input  C,
  output y,
  output not_y
);

  D_Flip_Flop #(.trigger("high")) d_ff_1 (.D(F), .clk(C), .Q(y), .Qn(not_y));  // open: preset, reset
endmodule

module FF_FAC (
  input  F,
  input  A,
  input  C,
  output y,
  output not_y
);

  wire and_1_out;

  FF_FC ff_fc_1 (.F(F), .C(and_1_out), .y(y), .not_y(not_y));
  and and_1 (and_1_out, A, C);
endmodule

module Registro_8bit (
  input  A,
  input  C,
  input  [7:0] x,
  output [7:0] y
);

  FF_FAC ff_fac_1 (.F(x[0]), .A(A), .C(C), .y(y[0]));  // open: not_y
  FF_FAC ff_fac_2 (.F(x[1]), .A(A), .C(C), .y(y[1]));  // open: not_y
  FF_FAC ff_fac_3 (.F(x[2]), .A(A), .C(C), .y(y[2]));  // open: not_y
  FF_FAC ff_fac_4 (.F(x[3]), .A(A), .C(C), .y(y[3]));  // open: not_y
  FF_FAC ff_fac_5 (.F(x[4]), .A(A), .C(C), .y(y[4]));  // open: not_y
  FF_FAC ff_fac_6 (.F(x[5]), .A(A), .C(C), .y(y[5]));  // open: not_y
  FF_FAC ff_fac_7 (.F(x[6]), .A(A), .C(C), .y(y[6]));  // open: not_y
  FF_FAC ff_fac_8 (.F(x[7]), .A(A), .C(C), .y(y[7]));  // open: not_y
endmodule

module FullAdder (
  input  a,
  input  b,
  input  r_in,
  output S,
  output r_out
);

  wire and_1_out, and_2_out, and_3_out;

  and and_1 (and_1_out, a, b);
  and and_2 (and_2_out, b, r_in);
  and and_3 (and_3_out, r_in, a);
  xor xor_1 (S, a, b, r_in);
  or or_1 (r_out, and_1_out, and_2_out, and_3_out);
endmodule

module myAdder (
  input  [7:0] B,
  input  [7:0] A,
  input  r_in,
  output r_out,
  output [7:0] S
);

  wire fulladder_1_r_out, fulladder_2_r_out, fulladder_3_r_out, fulladder_4_r_out, fulladder_5_r_out,
       fulladder_6_r_out, fulladder_7_r_out;

  FullAdder fulladder_1 (.a(B[0]), .b(A[0]), .r_in(r_in), .S(S[0]), .r_out(fulladder_1_r_out));
  FullAdder fulladder_2 (.a(B[1]), .b(A[1]), .r_in(fulladder_1_r_out), .S(S[1]), .r_out(fulladder_2_r_out));
  FullAdder fulladder_3 (.a(B[2]), .b(A[2]), .r_in(fulladder_2_r_out), .S(S[2]), .r_out(fulladder_3_r_out));
  FullAdder fulladder_4 (.a(B[3]), .b(A[3]), .r_in(fulladder_3_r_out), .S(S[3]), .r_out(fulladder_4_r_out));
  FullAdder fulladder_5 (.a(B[4]), .b(A[4]), .r_in(fulladder_4_r_out), .S(S[4]), .r_out(fulladder_5_r_out));
  FullAdder fulladder_6 (.a(B[5]), .b(A[5]), .r_in(fulladder_5_r_out), .S(S[5]), .r_out(fulladder_6_r_out));
  FullAdder fulladder_7 (.a(B[6]), .b(A[6]), .r_in(fulladder_6_r_out), .S(S[6]), .r_out(fulladder_7_r_out));
  FullAdder fulladder_8 (.a(B[7]), .b(A[7]), .r_in(fulladder_7_r_out), .S(S[7]), .r_out(r_out));
endmodule

module ALU (
  input  [7:0] A,
  input  [7:0] B,
  input  x1,
  input  x0,
  input  r_in,
  input  C,
  output [7:0] ris,
  output [3:0] flags
);

  wire and_1_out, myadder_1_r_out, nor_1_out, xnor_1_out, xor_1_out;
  wire [1:0] and_10_out;
  wire [7:0] and_9_out, and_19_out, multiplexer_1_out, myadder_1_s, not_8_out, or_8_out;

  xnor xnor_1 (xnor_1_out, multiplexer_1_out[7], and_9_out[7]);
  and and_1 (and_1_out, xnor_1_out, xor_1_out);
  xor xor_1 (xor_1_out, multiplexer_1_out[7], ris[7]);
  FF_FC ovf (.F(and_1_out), .C(C), .y(flags[3]));  // open: not_y
  not not_1 (not_8_out[7], B[7]);
  not not_2 (not_8_out[6], B[6]);
  not not_3 (not_8_out[5], B[5]);
  not not_4 (not_8_out[4], B[4]);
  not not_5 (not_8_out[3], B[3]);
  Multiplexer #(.width(8)) multiplexer_1 (.in0(B), .in1(not_8_out), .out(multiplexer_1_out), .sel(x0));
  myAdder myadder_1 (.r_in(r_in), .A(and_9_out), .B(multiplexer_1_out), .S(myadder_1_s), .r_out(myadder_1_r_out));
  FF_FC r_out (.F(myadder_1_r_out), .C(C), .y(flags[2]));  // open: not_y
  not not_6 (not_8_out[2], B[2]);
  not not_7 (not_8_out[1], B[1]);
  not not_8 (not_8_out[0], B[0]);
  Multiplexer #(.select(2), .width(8)) multiplexer_2 (
    .in0(myadder_1_s), .in1(and_19_out), .in2(or_8_out), .out(ris), .sel(and_10_out));  // open: in3
  FF_FC S (.F(ris[7]), .C(C), .y(flags[1]));  // open: not_y
  FF_FC Z (.F(nor_1_out), .C(C), .y(flags[0]));  // open: not_y
  and and_2 (and_9_out[7], x1, A[7]);
  and and_3 (and_9_out[6], x1, A[6]);
  nor nor_1 (nor_1_out, ris[7], ris[6], ris[5], ris[4], ris[3], ris[2], ris[1], ris[0]);
  and and_4 (and_9_out[5], x1, A[5]);
  and and_5 (and_9_out[4], x1, A[4]);
  and and_6 (and_9_out[3], x1, A[3]);
  and and_7 (and_9_out[2], x1, A[2]);
  and and_8 (and_9_out[1], x1, A[1]);
  and and_9 (and_9_out[0], x1, A[0]);
  and and_10 (and_10_out[0], ~x0, x1, r_in);  // AND_Gate
  and and_11 (and_10_out[1], x0, x1, ~r_in);  // AND_Gate
  and and_12 (and_19_out[7], A[7], B[7]);
  and and_13 (and_19_out[6], A[6], B[6]);
  and and_14 (and_19_out[5], A[5], B[5]);
  and and_15 (and_19_out[4], A[4], B[4]);
  and and_16 (and_19_out[3], A[3], B[3]);
  and and_17 (and_19_out[2], A[2], B[2]);
  and and_18 (and_19_out[1], A[1], B[1]);
  and and_19 (and_19_out[0], A[0], B[0]);
  or or_1 (or_8_out[7], A[7], B[7]);
  or or_2 (or_8_out[6], A[6], B[6]);
  or or_3 (or_8_out[5], A[5], B[5]);
  or or_4 (or_8_out[4], A[4], B[4]);
  or or_5 (or_8_out[3], A[3], B[3]);
  or or_6 (or_8_out[2], A[2], B[2]);
  or or_7 (or_8_out[1], A[1], B[1]);
  or or_8 (or_8_out[0], A[0], B[0]);
endmodule

module MBR (
  input  [7:0] mbr_in,
  input  A_mbr,
  input  L,
  input  C,
  input  [7:0] ext,
  output [7:0] mbr_out
);

  wire multiplexer_1_out, multiplexer_2_out, multiplexer_3_out, multiplexer_4_out, multiplexer_5_out,
       multiplexer_6_out, multiplexer_7_out, multiplexer_8_out;

  Multiplexer multiplexer_1 (.in0(ext[7]), .in1(mbr_in[7]), .out(multiplexer_1_out), .sel(L));
  FF_MS ff_ms_1 (.A(A_mbr), .C(C), .F(multiplexer_1_out), .y(mbr_out[7]));  // open: not_y
  FF_MS ff_ms_2 (.A(A_mbr), .C(C), .F(multiplexer_2_out), .y(mbr_out[6]));  // open: not_y
  Multiplexer multiplexer_2 (.in0(ext[6]), .in1(mbr_in[6]), .out(multiplexer_2_out), .sel(L));
  FF_MS ff_ms_3 (.A(A_mbr), .C(C), .F(multiplexer_3_out), .y(mbr_out[5]));  // open: not_y
  Multiplexer multiplexer_3 (.in0(ext[5]), .in1(mbr_in[5]), .out(multiplexer_3_out), .sel(L));
  FF_MS ff_ms_4 (.A(A_mbr), .C(C), .F(multiplexer_4_out), .y(mbr_out[4]));  // open: not_y
  Multiplexer multiplexer_4 (.in0(ext[4]), .in1(mbr_in[4]), .out(multiplexer_4_out), .sel(L));
  FF_MS ff_ms_5 (.A(A_mbr), .C(C), .F(multiplexer_5_out), .y(mbr_out[3]));  // open: not_y
  Multiplexer multiplexer_5 (.in0(ext[3]), .in1(mbr_in[3]), .out(multiplexer_5_out), .sel(L));
  Multiplexer multiplexer_6 (.in0(ext[2]), .in1(mbr_in[2]), .out(multiplexer_6_out), .sel(L));
  FF_MS ff_ms_6 (.A(A_mbr), .C(C), .F(multiplexer_6_out), .y(mbr_out[2]));  // open: not_y
  FF_MS ff_ms_7 (.A(A_mbr), .C(C), .F(multiplexer_7_out), .y(mbr_out[1]));  // open: not_y
  Multiplexer multiplexer_7 (.in0(ext[1]), .in1(mbr_in[1]), .out(multiplexer_7_out), .sel(L));
  FF_MS ff_ms_8 (.A(A_mbr), .C(C), .F(multiplexer_8_out), .y(mbr_out[0]));  // open: not_y
  Multiplexer multiplexer_8 (.in0(ext[0]), .in1(mbr_in[0]), .out(multiplexer_8_out), .sel(L));
endmodule

module Locazione_8bit (
  input  [7:0] in_locazioni,
  input  linea,
  input  S,
  input  [7:0] in_MBR,
  output [7:0] out_locazioni,
  output [7:0] out_MBR,
  output [7:0] value
);

  wire and_1_out, and_2_out, and_3_out, and_4_out, and_5_out, and_6_out, and_7_out, and_8_out, and_9_out,
       and_10_out, and_11_out, and_12_out, and_13_out, and_14_out, and_15_out, and_16_out;

  FF_FAC ff_fac_1 (.F(in_MBR[7]), .A(and_1_out), .C(1'b1), .y(value[7]));  // open: not_y
  and and_1 (and_1_out, linea, S);
  and and_2 (and_2_out, linea, value[7]);
  or or_1 (out_MBR[7], and_2_out, in_locazioni[7]);
  and and_3 (and_3_out, linea, S);
  FF_FAC ff_fac_2 (.F(in_MBR[6]), .A(and_3_out), .C(1'b1), .y(value[6]));  // open: not_y
  and and_4 (and_4_out, linea, value[6]);
  or or_2 (out_MBR[6], and_4_out, in_locazioni[6]);
  FF_FAC ff_fac_3 (.F(in_MBR[5]), .A(and_5_out), .C(1'b1), .y(value[5]));  // open: not_y
  and and_5 (and_5_out, linea, S);
  and and_6 (and_6_out, linea, value[5]);
  or or_3 (out_MBR[5], and_6_out, in_locazioni[5]);
  and and_7 (and_7_out, linea, S);
  FF_FAC ff_fac_4 (.F(in_MBR[4]), .A(and_7_out), .C(1'b1), .y(value[4]));  // open: not_y
  and and_8 (and_8_out, linea, value[4]);
  or or_4 (out_MBR[4], and_8_out, in_locazioni[4]);
  FF_FAC ff_fac_5 (.F(in_MBR[3]), .A(and_9_out), .C(1'b1), .y(value[3]));  // open: not_y
  and and_9 (and_9_out, linea, S);
  and and_10 (and_10_out, linea, value[3]);
  or or_5 (out_MBR[3], and_10_out, in_locazioni[3]);
  and and_11 (and_11_out, linea, S);
  FF_FAC ff_fac_6 (.F(in_MBR[2]), .A(and_11_out), .C(1'b1), .y(value[2]));  // open: not_y
  and and_12 (and_12_out, linea, value[2]);
  or or_6 (out_MBR[2], and_12_out, in_locazioni[2]);
  FF_FAC ff_fac_7 (.F(in_MBR[1]), .A(and_13_out), .C(1'b1), .y(value[1]));  // open: not_y
  and and_13 (and_13_out, linea, S);
  and and_14 (and_14_out, linea, value[1]);
  or or_7 (out_MBR[1], and_14_out, in_locazioni[1]);
  and and_15 (and_15_out, linea, S);
  FF_FAC ff_fac_8 (.F(in_MBR[0]), .A(and_15_out), .C(1'b1), .y(value[0]));  // open: not_y
  and and_16 (and_16_out, linea, value[0]);
  or or_8 (out_MBR[0], and_16_out, in_locazioni[0]);

  assign out_locazioni = in_MBR;
endmodule

module Registro_4bit (
  input  A,
  input  C,
  input  [3:0] x,
  output [3:0] y
);

  FF_FAC ff_fac_1 (.F(x[0]), .A(A), .C(C), .y(y[0]));  // open: not_y
  FF_FAC ff_fac_2 (.F(x[1]), .A(A), .C(C), .y(y[1]));  // open: not_y
  FF_FAC ff_fac_3 (.F(x[2]), .A(A), .C(C), .y(y[2]));  // open: not_y
  FF_FAC ff_fac_4 (.F(x[3]), .A(A), .C(C), .y(y[3]));  // open: not_y
endmodule

module RAM_16byte (
  input  S,
  input  A_mar,
  input  S_ext,
  input  A_mar_ext,
  input  [3:0] in_mar,
  input  inc_mar,
  input  [3:0] in_mar_ext,
  input  ext,
  input  [7:0] in_mbr,
  input  [7:0] in_mbr_ext,
  input  L,
  input  A_mbr,
  input  C,
  input  A_mbr_ext,
  input  C_ext,
  output [7:0] l_0,
  output [7:0] l_1,
  output [7:0] l_2,
  output [7:0] l_3,
  output [7:0] l_4,
  output [7:0] l_5,
  output [7:0] l_6,
  output [7:0] l_7,
  output [7:0] l_8,
  output [7:0] l_9,
  output [7:0] l_10,
  output [7:0] l_11,
  output [7:0] l_12,
  output [7:0] l_13,
  output [7:0] l_14,
  output [7:0] l_15,
  output [7:0] out_mbr
);

  wire and_1_out, C_t, decoder_1_out0, decoder_1_out1, decoder_1_out2, decoder_1_out3, decoder_1_out4,
       decoder_1_out5, decoder_1_out6, decoder_1_out7, decoder_1_out8, decoder_1_out9, decoder_1_out10,
       decoder_1_out11, decoder_1_out12, decoder_1_out13, decoder_1_out14, decoder_1_out15,
       multiplexer_2_out, multiplexer_4_out, multiplexer_6_out;
  wire [3:0] mar_1_y, multiplexer_1_out;
  wire [7:0] locazione_8bit_1_out_mbr, locazione_8bit_2_out_locazioni, locazione_8bit_2_out_mbr,
       locazione_8bit_3_out_locazioni, locazione_8bit_3_out_mbr, locazione_8bit_4_out_locazioni,
       locazione_8bit_4_out_mbr, locazione_8bit_5_out_locazioni, locazione_8bit_5_out_mbr,
       locazione_8bit_6_out_locazioni, locazione_8bit_6_out_mbr, locazione_8bit_7_out_locazioni,
       locazione_8bit_7_out_mbr, locazione_8bit_8_out_locazioni, locazione_8bit_8_out_mbr,
       locazione_8bit_9_out_locazioni, locazione_8bit_9_out_mbr, locazione_8bit_10_out_locazioni,
       locazione_8bit_10_out_mbr, locazione_8bit_11_out_locazioni, locazione_8bit_11_out_mbr,
       locazione_8bit_12_out_locazioni, locazione_8bit_12_out_mbr, locazione_8bit_13_out_locazioni,
       locazione_8bit_13_out_mbr, locazione_8bit_14_out_locazioni, locazione_8bit_14_out_mbr,
       locazione_8bit_15_out_locazioni, locazione_8bit_15_out_mbr, locazione_8bit_16_out_locazioni,
       locazione_8bit_16_out_mbr, multiplexer_5_out;

  Multiplexer #(.width(4)) multiplexer_1 (.in0(in_mar), .in1(in_mar_ext), .out(multiplexer_1_out), .sel(ext));
  MAR mar_1 (.x(multiplexer_1_out), .A(multiplexer_2_out), .C(C_t), .inc(inc_mar), .y(mar_1_y));
  Multiplexer multiplexer_2 (.in0(A_mar), .in1(A_mar_ext), .out(multiplexer_2_out), .sel(ext));
  Multiplexer multiplexer_3 (.in0(C), .in1(C_ext), .out(C_t), .sel(ext));
  Decoder #(.enable("false"), .select(4)) decoder_1 (
    .out0(decoder_1_out0), .out1(decoder_1_out1), .out2(decoder_1_out2), .out3(decoder_1_out3),
    .out4(decoder_1_out4), .out5(decoder_1_out5), .out6(decoder_1_out6), .out7(decoder_1_out7),
    .out8(decoder_1_out8), .out9(decoder_1_out9), .out10(decoder_1_out10), .out11(decoder_1_out11),
    .out12(decoder_1_out12), .out13(decoder_1_out13), .out14(decoder_1_out14), .out15(decoder_1_out15),
    .sel(mar_1_y));
  Locazione_8bit locazione_8bit_1 (
    .in_MBR(locazione_8bit_2_out_locazioni), .in_locazioni({8{1'b0}}), .S(and_1_out), .linea(decoder_1_out0),
    .out_MBR(locazione_8bit_1_out_mbr), .value(l_0));  // open: out_locazioni
  Locazione_8bit locazione_8bit_2 (
    .in_MBR(locazione_8bit_3_out_locazioni), .in_locazioni(locazione_8bit_1_out_mbr), .S(and_1_out),
    .linea(decoder_1_out1), .out_locazioni(locazione_8bit_2_out_locazioni),
    .out_MBR(locazione_8bit_2_out_mbr), .value(l_1));
  Locazione_8bit locazione_8bit_3 (
    .in_MBR(locazione_8bit_4_out_locazioni), .in_locazioni(locazione_8bit_2_out_mbr), .S(and_1_out),
    .linea(decoder_1_out2), .out_locazioni(locazione_8bit_3_out_locazioni),
    .out_MBR(locazione_8bit_3_out_mbr), .value(l_2));
  Locazione_8bit locazione_8bit_4 (
    .in_MBR(locazione_8bit_5_out_locazioni), .in_locazioni(locazione_8bit_3_out_mbr), .S(and_1_out),
    .linea(decoder_1_out3), .out_locazioni(locazione_8bit_4_out_locazioni),
    .out_MBR(locazione_8bit_4_out_mbr), .value(l_3));
  Locazione_8bit locazione_8bit_5 (
    .in_MBR(locazione_8bit_6_out_locazioni), .in_locazioni(locazione_8bit_4_out_mbr), .S(and_1_out),
    .linea(decoder_1_out4), .out_locazioni(locazione_8bit_5_out_locazioni),
    .out_MBR(locazione_8bit_5_out_mbr), .value(l_4));
  Locazione_8bit locazione_8bit_6 (
    .in_MBR(locazione_8bit_7_out_locazioni), .in_locazioni(locazione_8bit_5_out_mbr), .S(and_1_out),
    .linea(decoder_1_out5), .out_locazioni(locazione_8bit_6_out_locazioni),
    .out_MBR(locazione_8bit_6_out_mbr), .value(l_5));
  Locazione_8bit locazione_8bit_7 (
    .in_MBR(locazione_8bit_8_out_locazioni), .in_locazioni(locazione_8bit_6_out_mbr), .S(and_1_out),
    .linea(decoder_1_out6), .out_locazioni(locazione_8bit_7_out_locazioni),
    .out_MBR(locazione_8bit_7_out_mbr), .value(l_6));
  Locazione_8bit locazione_8bit_8 (
    .in_MBR(locazione_8bit_9_out_locazioni), .in_locazioni(locazione_8bit_7_out_mbr), .S(and_1_out),
    .linea(decoder_1_out7), .out_locazioni(locazione_8bit_8_out_locazioni),
    .out_MBR(locazione_8bit_8_out_mbr), .value(l_7));
  Locazione_8bit locazione_8bit_9 (
    .in_MBR(locazione_8bit_10_out_locazioni), .in_locazioni(locazione_8bit_8_out_mbr), .S(and_1_out),
    .linea(decoder_1_out8), .out_locazioni(locazione_8bit_9_out_locazioni),
    .out_MBR(locazione_8bit_9_out_mbr), .value(l_8));
  Locazione_8bit locazione_8bit_10 (
    .in_MBR(locazione_8bit_11_out_locazioni), .in_locazioni(locazione_8bit_9_out_mbr), .S(and_1_out),
    .linea(decoder_1_out9), .out_locazioni(locazione_8bit_10_out_locazioni),
    .out_MBR(locazione_8bit_10_out_mbr), .value(l_9));
  Locazione_8bit locazione_8bit_11 (
    .in_MBR(locazione_8bit_12_out_locazioni), .in_locazioni(locazione_8bit_10_out_mbr), .S(and_1_out),
    .linea(decoder_1_out10), .out_locazioni(locazione_8bit_11_out_locazioni),
    .out_MBR(locazione_8bit_11_out_mbr), .value(l_10));
  Locazione_8bit locazione_8bit_12 (
    .in_MBR(locazione_8bit_13_out_locazioni), .in_locazioni(locazione_8bit_11_out_mbr), .S(and_1_out),
    .linea(decoder_1_out11), .out_locazioni(locazione_8bit_12_out_locazioni),
    .out_MBR(locazione_8bit_12_out_mbr), .value(l_11));
  Locazione_8bit locazione_8bit_13 (
    .in_MBR(locazione_8bit_14_out_locazioni), .in_locazioni(locazione_8bit_12_out_mbr), .S(and_1_out),
    .linea(decoder_1_out12), .out_locazioni(locazione_8bit_13_out_locazioni),
    .out_MBR(locazione_8bit_13_out_mbr), .value(l_12));
  Locazione_8bit locazione_8bit_14 (
    .in_MBR(locazione_8bit_15_out_locazioni), .in_locazioni(locazione_8bit_13_out_mbr), .S(and_1_out),
    .linea(decoder_1_out13), .out_locazioni(locazione_8bit_14_out_locazioni),
    .out_MBR(locazione_8bit_14_out_mbr), .value(l_13));
  Locazione_8bit locazione_8bit_15 (
    .in_MBR(locazione_8bit_16_out_locazioni), .in_locazioni(locazione_8bit_14_out_mbr), .S(and_1_out),
    .linea(decoder_1_out14), .out_locazioni(locazione_8bit_15_out_locazioni),
    .out_MBR(locazione_8bit_15_out_mbr), .value(l_14));
  Locazione_8bit locazione_8bit_16 (
    .in_MBR(out_mbr), .in_locazioni(locazione_8bit_15_out_mbr), .S(and_1_out), .linea(decoder_1_out15),
    .out_locazioni(locazione_8bit_16_out_locazioni), .out_MBR(locazione_8bit_16_out_mbr), .value(l_15));
  MBR mbr_1 (
    .A_mbr(multiplexer_4_out), .L(L), .C(C_t), .mbr_in(locazione_8bit_16_out_mbr), .ext(multiplexer_5_out),
    .mbr_out(out_mbr));
  Multiplexer multiplexer_4 (.in0(A_mbr), .in1(A_mbr_ext), .out(multiplexer_4_out), .sel(ext));
  Multiplexer #(.width(8)) multiplexer_5 (.in0(in_mbr), .in1(in_mbr_ext), .out(multiplexer_5_out), .sel(ext));
  and and_1 (and_1_out, multiplexer_6_out, C_t);
  Multiplexer multiplexer_6 (.in0(S), .in1(S_ext), .out(multiplexer_6_out), .sel(ext));
endmodule

module FF_MS (
  input  F,
  input  A,
  input  C,
  output y,
  output not_y
);

  wire ff_fc_1_y, multiplexer_1_out, not_1_out;

  Multiplexer multiplexer_1 (.in0(ff_fc_1_y), .in1(F), .out(multiplexer_1_out), .sel(A));
  FF_FC ff_fc_1 (.F(multiplexer_1_out), .C(C), .y(ff_fc_1_y));  // open: not_y
  FF_FC ff_fc_2 (.F(ff_fc_1_y), .C(not_1_out), .y(y), .not_y(not_y));
  not not_1 (not_1_out, C);
endmodule

module Registro_MS_8bit (
  input  A,
  input  C,
  input  [7:0] x,
  output [7:0] y
);

  FF_MS ff_ms_1 (.A(A), .C(C), .F(x[0]), .y(y[0]));  // open: not_y
  FF_MS ff_ms_2 (.A(A), .C(C), .F(x[1]), .y(y[1]));  // open: not_y
  FF_MS ff_ms_3 (.A(A), .C(C), .F(x[2]), .y(y[2]));  // open: not_y
  FF_MS ff_ms_4 (.A(A), .C(C), .F(x[3]), .y(y[3]));  // open: not_y
  FF_MS ff_ms_5 (.A(A), .C(C), .F(x[4]), .y(y[4]));  // open: not_y
  FF_MS ff_ms_6 (.A(A), .C(C), .F(x[5]), .y(y[5]));  // open: not_y
  FF_MS ff_ms_7 (.A(A), .C(C), .F(x[6]), .y(y[6]));  // open: not_y
  FF_MS ff_ms_8 (.A(A), .C(C), .F(x[7]), .y(y[7]));  // open: not_y
endmodule

module Registro_MS_4bit (
  input  A,
  input  C,
  input  [3:0] x,
  output [3:0] y
);

  FF_MS ff_ms_1 (.A(A), .C(C), .F(x[0]), .y(y[0]));  // open: not_y
  FF_MS ff_ms_2 (.A(A), .C(C), .F(x[1]), .y(y[1]));  // open: not_y
  FF_MS ff_ms_3 (.A(A), .C(C), .F(x[2]), .y(y[2]));  // open: not_y
  FF_MS ff_ms_4 (.A(A), .C(C), .F(x[3]), .y(y[3]));  // open: not_y
endmodule

module Half_Adder (
  input  A,
  input  C,
  output S,
  output R
);

  xor xor_1 (S, A, C);
  and and_1 (R, A, C);
endmodule

module function_add1 (
  input  [7:0] A,
  output [7:0] S
);

  wire half_adder_2_r, half_adder_3_r, half_adder_4_r, half_adder_5_r, half_adder_6_r, half_adder_7_r,
       half_adder_8_r;

  Half_Adder half_adder_1 (.A(A[7]), .C(half_adder_2_r), .S(S[7]));  // open: R
  Half_Adder half_adder_2 (.A(A[6]), .C(half_adder_3_r), .R(half_adder_2_r), .S(S[6]));
  Half_Adder half_adder_3 (.A(A[5]), .C(half_adder_4_r), .R(half_adder_3_r), .S(S[5]));
  Half_Adder half_adder_4 (.A(A[4]), .C(half_adder_5_r), .R(half_adder_4_r), .S(S[4]));
  Half_Adder half_adder_5 (.A(A[3]), .C(half_adder_6_r), .R(half_adder_5_r), .S(S[3]));
  Half_Adder half_adder_6 (.A(A[2]), .C(half_adder_7_r), .R(half_adder_6_r), .S(S[2]));
  Half_Adder half_adder_7 (.A(A[1]), .C(half_adder_8_r), .R(half_adder_7_r), .S(S[1]));
  Half_Adder half_adder_8 (.A(A[0]), .C(1'b1), .R(half_adder_8_r), .S(S[0]));
endmodule

module Half_Subtracter (
  input  A,
  input  D,
  output S,
  output P
);

  wire not_1_out;

  not not_1 (not_1_out, A);
  xor xor_1 (S, A, D);
  and and_1 (P, not_1_out, D);
endmodule

module function_sub1 (
  input  [7:0] A,
  output [7:0] S
);

  wire half_subtracter_2_p, half_subtracter_3_p, half_subtracter_4_p, half_subtracter_5_p,
       half_subtracter_6_p, half_subtracter_7_p, half_subtracter_8_p;

  Half_Subtracter half_subtracter_1 (.A(A[7]), .D(half_subtracter_2_p), .S(S[7]));  // open: P
  Half_Subtracter half_subtracter_2 (.A(A[6]), .D(half_subtracter_3_p), .S(S[6]), .P(half_subtracter_2_p));
  Half_Subtracter half_subtracter_3 (.A(A[5]), .D(half_subtracter_4_p), .S(S[5]), .P(half_subtracter_3_p));
  Half_Subtracter half_subtracter_4 (.A(A[4]), .D(half_subtracter_5_p), .S(S[4]), .P(half_subtracter_4_p));
  Half_Subtracter half_subtracter_5 (.A(A[3]), .D(half_subtracter_6_p), .S(S[3]), .P(half_subtracter_5_p));
  Half_Subtracter half_subtracter_6 (.A(A[2]), .D(half_subtracter_7_p), .S(S[2]), .P(half_subtracter_6_p));
  Half_Subtracter half_subtracter_7 (.A(A[1]), .D(half_subtracter_8_p), .S(S[1]), .P(half_subtracter_7_p));
  Half_Subtracter half_subtracter_8 (.A(A[0]), .D(1'b1), .S(S[0]), .P(half_subtracter_8_p));
endmodule

module function_SHL (
  input  [7:0] A,
  output [7:0] S
);


  assign S = {A[6:0], 1'b0};
endmodule

module function_SHR (
  input  [7:0] A,
  output [7:0] S
);


  assign S = {1'b0, A[7:1]};
endmodule

module R_fun_T1 (
  input  A,
  input  C,
  input  T1_1,
  input  T1_0,
  input  [7:0] x,
  output [7:0] y,
  output OR_T1
);

  wire [7:0] function_add1_1_s, function_shl_1_s, function_sub1_1_s, multiplexer_1_out;

  function_SHL function_shl_1 (.A(y), .S(function_shl_1_s));
  function_sub1 function_sub1_1 (.A(y), .S(function_sub1_1_s));
  function_add1 function_add1_1 (.A(y), .S(function_add1_1_s));
  Registro_MS_8bit registro_ms_8bit_1 (.A(A), .C(C), .x(multiplexer_1_out), .y(y));
  Multiplexer #(.select(2), .width(8)) multiplexer_1 (
    .in0(x), .in1(function_add1_1_s), .in2(function_sub1_1_s), .in3(function_shl_1_s),
    .out(multiplexer_1_out), .sel({T1_1, T1_0}));
  or or_1 (OR_T1, y[0], y[1], y[2], y[3], y[4], y[5], y[6], y[7]);
endmodule

module R_fun_T2 (
  input  A,
  input  C,
  input  T1_1,
  input  T1_0,
  input  [7:0] x,
  output [7:0] y,
  output OR_T2
);

  wire [7:0] function_add1_1_s, function_shr_1_s, function_sub1_1_s, multiplexer_1_out;

  function_SHR function_shr_1 (.A(y), .S(function_shr_1_s));
  function_sub1 function_sub1_1 (.A(y), .S(function_sub1_1_s));
  function_add1 function_add1_1 (.A(y), .S(function_add1_1_s));
  Registro_MS_8bit registro_ms_8bit_1 (.A(A), .C(C), .x(multiplexer_1_out), .y(y));
  Multiplexer #(.select(2), .width(8)) multiplexer_1 (
    .in0(x), .in1(function_add1_1_s), .in2(function_sub1_1_s), .in3(function_shr_1_s),
    .out(multiplexer_1_out), .sel({T1_1, T1_0}));
  or or_1 (OR_T2, y[0], y[1], y[2], y[3], y[4], y[5], y[6], y[7]);
endmodule

module PC (
  input  A,
  input  C,
  input  k0,
  input  k1,
  input  [3:0] x,
  output [3:0] y
);

  wire [3:0] fun_4bitadd1_1_s, multiplexer_1_out;

  fun_4bitAdd1 fun_4bitadd1_1 (.A(y), .S(fun_4bitadd1_1_s));
  Registro_MS_4bit registro_ms_4bit_1 (.A(A), .C(C), .x(multiplexer_1_out), .y(y));
  Multiplexer #(.select(2), .width(4)) multiplexer_1 (
    .in0(x), .in1(fun_4bitadd1_1_s), .in2(4'b0000), .out(multiplexer_1_out), .sel({k1, k0}));  // open: in3
endmodule

module fun_4bitAdd1 (
  input  [3:0] A,
  output [3:0] S
);

  wire half_adder_2_r, half_adder_3_r, half_adder_4_r;

  Half_Adder half_adder_1 (.A(A[3]), .C(half_adder_2_r), .S(S[3]));  // open: R
  Half_Adder half_adder_2 (.A(A[2]), .C(half_adder_3_r), .R(half_adder_2_r), .S(S[2]));
  Half_Adder half_adder_3 (.A(A[1]), .C(half_adder_4_r), .R(half_adder_3_r), .S(S[1]));
  Half_Adder half_adder_4 (.A(A[0]), .C(1'b1), .R(half_adder_4_r), .S(S[0]));
endmodule

module Accumulatore (
  input  A,
  input  C,
  input  [7:0] x,
  output or_AC,
  output [7:0] y
);

  Registro_MS_8bit registro_ms_8bit_1 (.A(A), .C(C), .x(x), .y(y));
  or or_1 (or_AC, y[0], y[1], y[2], y[3], y[4], y[5], y[6], y[7]);
endmodule

module IR (
  input  A,
  input  C,
  input  [7:0] x,
  input  z,
  output [3:0] cop,
  output [3:0] ind
);

  wire [7:0] multiplexer_1_out;

  Registro_MS_8bit registro_ms_8bit_1 (.A(A), .C(C), .x(multiplexer_1_out), .y({cop, ind}));
  Multiplexer #(.width(8)) multiplexer_1 (.in0(x), .in1({8{1'b0}}), .out(multiplexer_1_out), .sel(z));
endmodule

module EXT (
  input  [3:0] x,
  input  k,
  output [7:0] y
);

  Multiplexer #(.width(8)) multiplexer_1 (.in0({4'b0000, x}), .in1({{5{x[3]}}, x[2:0]}), .out(y), .sel(k));
endmodule

module Parte_Controllo_ROM (
  input  [3:0] istruzione,
  input  b_ACC,
  input  b_T1,
  input  b_T2,
  input  reset,
  input  in_6,
  output [38:0] s_alpha
);

  wire and_1_out, and_2_out, and_3_out, and_4_out, and_5_out, and_6_out, and_7_out, and_8_out, and_9_out,
       and_10_out, and_11_out, and_12_out, and_13_out, and_14_out, and_15_out, and_16_out, and_17_out,
       and_18_out, multiplexer_1_out, multiplexer_2_out, multiplexer_3_out, s0_out, s1_out, u0_out, u2_out,
       u4_out, u5_out, u11_out, u13_out, u14_out, u15_out, u16_out, u18_out, u21_out, u22_out, u24_out,
       u26_out, u27_out, u28_out, u29_out;
  wire [3:0] ff_ms_1_y;
  wire [38:0] a0_out;

  and u1 (a0_out[21], ~istruzione[3], ~istruzione[2], ~istruzione[1], ~istruzione[0], ~ff_ms_1_y[3], ~ff_ms_1_y[2], ~ff_ms_1_y[1], ~ff_ms_1_y[0]);  // AND_Gate
  and and_1 (and_1_out, ~istruzione[3], ~istruzione[2], ~istruzione[1], ~istruzione[0], ~ff_ms_1_y[3], ~ff_ms_1_y[2], ~ff_ms_1_y[1], ff_ms_1_y[0]);  // AND_Gate
  and u3 (a0_out[3], ~istruzione[3], ~istruzione[2], ~istruzione[1], ~istruzione[0], ~ff_ms_1_y[3], ~ff_ms_1_y[2], ff_ms_1_y[1], ~ff_ms_1_y[0]);  // AND_Gate
  and and_2 (and_2_out, ~istruzione[3], ~istruzione[2], ~istruzione[1], istruzione[0], ~ff_ms_1_y[3], ~ff_ms_1_y[2], ~ff_ms_1_y[1], ~ff_ms_1_y[0]);  // AND_Gate
  and and_3 (and_3_out, ~istruzione[3], ~istruzione[2], ~istruzione[1], istruzione[0], ~ff_ms_1_y[3], ~ff_ms_1_y[2], ~ff_ms_1_y[1], ff_ms_1_y[0]);  // AND_Gate
  and u5 (u5_out, ~istruzione[3], ~istruzione[2], ~istruzione[1], istruzione[0], ~ff_ms_1_y[3], ~ff_ms_1_y[2], ff_ms_1_y[1], ~ff_ms_1_y[0]);  // AND_Gate
  and u11 (u11_out, ~istruzione[3], ~istruzione[2], istruzione[1], ~istruzione[0], ~ff_ms_1_y[3], ~ff_ms_1_y[2], ~ff_ms_1_y[1], ~ff_ms_1_y[0]);  // AND_Gate
  and u12 (a0_out[7], ~istruzione[3], ~istruzione[2], istruzione[1], ~istruzione[0], ~ff_ms_1_y[3], ~ff_ms_1_y[2], ~ff_ms_1_y[1], ff_ms_1_y[0]);  // AND_Gate
  and and_4 (and_4_out, ~istruzione[3], ~istruzione[2], istruzione[1], istruzione[0], ~ff_ms_1_y[3], ~ff_ms_1_y[2], ~ff_ms_1_y[1], ~ff_ms_1_y[0]);  // AND_Gate
  and and_5 (and_5_out, ~istruzione[3], ~istruzione[2], istruzione[1], istruzione[0], ~ff_ms_1_y[3], ~ff_ms_1_y[2], ~ff_ms_1_y[1], ff_ms_1_y[0]);  // AND_Gate
  and and_6 (and_6_out, ~istruzione[3], ~istruzione[2], istruzione[1], istruzione[0], ~ff_ms_1_y[3], ~ff_ms_1_y[2], ff_ms_1_y[1], ~ff_ms_1_y[0]);  // AND_Gate
  and u15 (u15_out, ~istruzione[3], ~istruzione[2], istruzione[1], istruzione[0], ~ff_ms_1_y[3], ~ff_ms_1_y[2], ff_ms_1_y[1], ff_ms_1_y[0]);  // AND_Gate
  and and_7 (and_7_out, ~istruzione[3], istruzione[2], ~istruzione[1], ~istruzione[0], ~ff_ms_1_y[3], ~ff_ms_1_y[2], ~ff_ms_1_y[1], ~ff_ms_1_y[0]);  // AND_Gate
  and and_8 (and_8_out, ~istruzione[3], istruzione[2], ~istruzione[1], ~istruzione[0], ~ff_ms_1_y[3], ~ff_ms_1_y[2], ~ff_ms_1_y[1], ff_ms_1_y[0]);  // AND_Gate
  and and_9 (and_9_out, ~istruzione[3], istruzione[2], ~istruzione[1], ~istruzione[0], ~ff_ms_1_y[3], ~ff_ms_1_y[2], ff_ms_1_y[1], ~ff_ms_1_y[0]);  // AND_Gate
  and u16 (u16_out, ~istruzione[3], istruzione[2], ~istruzione[1], ~istruzione[0], ~ff_ms_1_y[3], ~ff_ms_1_y[2], ff_ms_1_y[1], ff_ms_1_y[0]);  // AND_Gate
  and and_10 (and_10_out, ~istruzione[3], istruzione[2], ~istruzione[1], istruzione[0], ~ff_ms_1_y[3], ~ff_ms_1_y[2], ~ff_ms_1_y[1], ~ff_ms_1_y[0]);  // AND_Gate
  and and_11 (and_11_out, ~istruzione[3], istruzione[2], istruzione[1], ~istruzione[0], ~ff_ms_1_y[3], ~ff_ms_1_y[2], ~ff_ms_1_y[1], ~ff_ms_1_y[0], ~b_ACC);  // AND_Gate
  and u0 (u0_out, ~istruzione[3], istruzione[2], istruzione[1], ~istruzione[0], ~ff_ms_1_y[3], ~ff_ms_1_y[2], ~ff_ms_1_y[1], ~ff_ms_1_y[0], b_ACC);  // AND_Gate
  and u18 (u18_out, ~istruzione[3], istruzione[2], istruzione[1], istruzione[0], ~ff_ms_1_y[3], ~ff_ms_1_y[2], ~ff_ms_1_y[1], ~ff_ms_1_y[0]);  // AND_Gate
  and u19 (a0_out[37], istruzione[3], ~istruzione[2], ~istruzione[1], ~istruzione[0], ~ff_ms_1_y[3], ~ff_ms_1_y[2], ~ff_ms_1_y[1], ~ff_ms_1_y[0]);  // AND_Gate
  and and_12 (and_12_out, istruzione[3], ~istruzione[2], ~istruzione[1], istruzione[0], ~ff_ms_1_y[3], ~ff_ms_1_y[2], ~ff_ms_1_y[1], ~ff_ms_1_y[0]);  // AND_Gate
  and u20 (a0_out[33], istruzione[3], ~istruzione[2], ~istruzione[1], istruzione[0], ~ff_ms_1_y[3], ~ff_ms_1_y[2], ~ff_ms_1_y[1], ff_ms_1_y[0]);  // AND_Gate
  and u21 (u21_out, istruzione[3], ~istruzione[2], ~istruzione[1], istruzione[0], ~ff_ms_1_y[3], ~ff_ms_1_y[2], ff_ms_1_y[1], ~ff_ms_1_y[0]);  // AND_Gate
  and u22 (u22_out, istruzione[3], ~istruzione[2], ~istruzione[1], istruzione[0], ~ff_ms_1_y[3], ~ff_ms_1_y[2], ff_ms_1_y[1], ff_ms_1_y[0], b_T1);  // AND_Gate
  and u23 (a0_out[16], istruzione[3], ~istruzione[2], ~istruzione[1], istruzione[0], ~ff_ms_1_y[3], ff_ms_1_y[2], ~ff_ms_1_y[1], ~ff_ms_1_y[0], b_T1);  // AND_Gate
  and u24 (u24_out, istruzione[3], ~istruzione[2], ~istruzione[1], istruzione[0], ~ff_ms_1_y[3], ~ff_ms_1_y[2], ff_ms_1_y[1], ff_ms_1_y[0], ~b_T1);  // AND_Gate
  and u25 (a0_out[36], istruzione[3], istruzione[2], istruzione[1], istruzione[0], ~ff_ms_1_y[3], ~ff_ms_1_y[2], ~ff_ms_1_y[1], ~ff_ms_1_y[0]);  // AND_Gate
  and and_13 (and_13_out, istruzione[3], ~istruzione[2], istruzione[1], ~istruzione[0], ~ff_ms_1_y[3], ~ff_ms_1_y[2], ~ff_ms_1_y[1], ~ff_ms_1_y[0]);  // AND_Gate
  and and_14 (and_14_out, istruzione[3], ~istruzione[2], istruzione[1], ~istruzione[0], ~ff_ms_1_y[3], ~ff_ms_1_y[2], ~ff_ms_1_y[1], ff_ms_1_y[0]);  // AND_Gate
  and and_15 (and_15_out, istruzione[3], ~istruzione[2], istruzione[1], ~istruzione[0], ~ff_ms_1_y[3], ~ff_ms_1_y[2], ff_ms_1_y[1], ~ff_ms_1_y[0]);  // AND_Gate
  and u26 (u26_out, istruzione[3], ~istruzione[2], istruzione[1], ~istruzione[0], ~ff_ms_1_y[3], ~ff_ms_1_y[2], ff_ms_1_y[1], ff_ms_1_y[0]);  // AND_Gate
  and and_16 (and_16_out, istruzione[3], ~istruzione[2], istruzione[1], istruzione[0], ~ff_ms_1_y[3], ~ff_ms_1_y[2], ~ff_ms_1_y[1], ~ff_ms_1_y[0]);  // AND_Gate
  and and_17 (and_17_out, istruzione[3], ~istruzione[2], istruzione[1], istruzione[0], ~ff_ms_1_y[3], ~ff_ms_1_y[2], ~ff_ms_1_y[1], ff_ms_1_y[0]);  // AND_Gate
  and and_18 (and_18_out, istruzione[3], ~istruzione[2], istruzione[1], istruzione[0], ~ff_ms_1_y[3], ~ff_ms_1_y[2], ff_ms_1_y[1], ~ff_ms_1_y[0]);  // AND_Gate
  and u27 (u27_out, istruzione[3], ~istruzione[2], istruzione[1], istruzione[0], ~ff_ms_1_y[3], ~ff_ms_1_y[2], ff_ms_1_y[1], ff_ms_1_y[0]);  // AND_Gate
  and u28 (u28_out, istruzione[3], istruzione[2], ~istruzione[1], ~istruzione[0], ~ff_ms_1_y[3], ~ff_ms_1_y[2], ~ff_ms_1_y[1], ~ff_ms_1_y[0]);  // AND_Gate
  and u29 (u29_out, istruzione[3], istruzione[2], ~istruzione[1], istruzione[0], ~ff_ms_1_y[3], ~ff_ms_1_y[2], ~ff_ms_1_y[1], ~ff_ms_1_y[0]);  // AND_Gate
  or s0 (s0_out, and_15_out, and_13_out, and_6_out, a0_out[21], and_2_out, u11_out, and_4_out, and_7_out, and_9_out, and_12_out, u21_out, a0_out[16], and_16_out, and_18_out);
  Multiplexer multiplexer_1 (.in0(s0_out), .in1(1'b0), .out(multiplexer_1_out), .sel(reset));
  FF_MS ff_ms_1 (.A(in_6), .C(in_6), .F(multiplexer_1_out), .y(ff_ms_1_y[0]));  // open: not_y
  or s1 (s1_out, and_15_out, and_14_out, and_1_out, and_3_out, and_5_out, and_6_out, and_8_out, and_9_out, a0_out[33], u21_out, a0_out[16], and_17_out, and_18_out);
  Multiplexer multiplexer_2 (.in0(s1_out), .in1(1'b0), .out(multiplexer_2_out), .sel(reset));
  FF_MS ff_ms_2 (.A(in_6), .C(in_6), .F(multiplexer_2_out), .y(ff_ms_1_y[1]));  // open: not_y
  Multiplexer multiplexer_3 (.in0(u22_out), .in1(1'b0), .out(multiplexer_3_out), .sel(reset));
  FF_MS ff_ms_3 (.A(in_6), .C(in_6), .F(multiplexer_3_out), .y(ff_ms_1_y[2]));  // open: not_y
  FF_MS ff_ms_4 (.A(in_6), .C(in_6), .F(1'b0), .y(ff_ms_1_y[3]));  // open: not_y
  or u4 (u4_out, and_2_out, and_12_out);
  or u2 (u2_out, and_1_out, and_17_out, and_3_out, and_5_out, and_14_out, and_8_out);
  or u13 (u13_out, and_4_out, and_16_out, and_13_out, and_7_out);
  or u14 (u14_out, and_6_out, and_18_out, and_15_out, and_9_out);
  or u17 (a0_out[23], and_10_out, and_11_out);
  or a0 (a0_out[0], u28_out, u26_out, a0_out[3], u0_out, u5_out, a0_out[7], u15_out, a0_out[23], u18_out, a0_out[37], u16_out, u24_out, u27_out, u29_out);
  or a1 (a0_out[1], u28_out, u26_out, u5_out, a0_out[7], u15_out, u0_out, u16_out, a0_out[23], u18_out, a0_out[37], u24_out, u27_out, u29_out);
  or a2 (a0_out[2], a0_out[3], a0_out[23]);
  or a4 (a0_out[4], u28_out, u26_out, u16_out, u18_out, u5_out, u15_out, u24_out, u27_out, u29_out);
  or a5 (a0_out[5], u4_out, u11_out, u13_out, a0_out[21], u22_out, u21_out, a0_out[33]);
  or a6 (a0_out[6], u2_out, u11_out, u22_out, u21_out, a0_out[33]);
  or a8 (a0_out[8], u2_out, u22_out, u21_out, a0_out[33]);
  or a10 (a0_out[10], u13_out, u22_out);
  or a11 (a0_out[11], u14_out, a0_out[16], a0_out[33]);
  or a12 (a0_out[12], u15_out, u26_out, a0_out[16], u27_out, u16_out);
  or a13 (a0_out[13], u16_out, u26_out);
  or a14 (a0_out[14], u16_out, u27_out);
  or a15 (a0_out[15], a0_out[16], u21_out);
  or a22 (a0_out[22], u4_out, u11_out, u28_out, u13_out, a0_out[23]);
  or a24 (a0_out[24], a0_out[21], u4_out, u11_out, u13_out);
  or a25 (a0_out[25], u26_out, u24_out, a0_out[16], u29_out, u16_out, u15_out, u27_out);
  or a26 (a0_out[26], u11_out, u13_out, u29_out, u18_out, a0_out[37]);
  or a27 (a0_out[27], a0_out[3], u5_out, u11_out, u13_out, u29_out, u14_out, a0_out[37], u21_out, u22_out);
  or a29 (a0_out[29], u28_out, u26_out, u5_out, u24_out, u14_out, u15_out, u16_out, u18_out, u13_out, a0_out[16], u22_out, u21_out, u27_out, u29_out);
  or a30 (a0_out[30], a0_out[3], u14_out, a0_out[37], u21_out, a0_out[16]);
  or a31 (a0_out[31], a0_out[3], u11_out, u13_out, u21_out, u22_out);
  or a32 (a0_out[32], u22_out, u21_out, a0_out[33]);
  or a34 (a0_out[34], u11_out, a0_out[21], u4_out, u13_out, a0_out[23], u28_out);
  or a35 (a0_out[35], u28_out, u27_out, a0_out[3], u5_out, u11_out, u13_out, u14_out, u15_out, u16_out, u18_out, a0_out[37], u21_out, u22_out, a0_out[16], u24_out, u26_out, u29_out);
  or a38 (a0_out[38], u15_out, u16_out, u26_out, u27_out);
  Multiplexer #(.width(39)) multiplexer_4 (
    .in0({a0_out[38:29], 1'b0, a0_out[27:21], 4'b0000, a0_out[16:10], 1'b0, a0_out[8:0]}), .in1({39{1'b0}}),
    .out(s_alpha), .sel(reset));

  // Notes on the sheet:
  //   FETCH
  //   LOAD
  //   STORE
  //   ADD
  //   SUB
  //   JUMP
  //   JUMPZ
  //   IN
  //   OUT
  //   SUM ARRAY
  //   HALT
  //   AND
  //   OR
  //   LOAD IMMEDIATE
  //   (unsigned)
  //   LOAD FLAGS
  //   s2
  //   s3
  //   a3
  //   a7
  //   a9
  //   a16
  //   a17
  //   a18
  //   a19
  //   a20
  //   a21
  //   a23
  //   a28
  //   a33
  //   a36
  //   a37
endmodule

module function_add1_4bit (
  input  [3:0] A,
  output [3:0] S
);

  wire half_adder_2_r, half_adder_3_r, half_adder_4_r;

  Half_Adder half_adder_1 (.A(A[3]), .C(half_adder_2_r), .S(S[3]));  // open: R
  Half_Adder half_adder_2 (.A(A[2]), .C(half_adder_3_r), .R(half_adder_2_r), .S(S[2]));
  Half_Adder half_adder_3 (.A(A[1]), .C(half_adder_4_r), .R(half_adder_3_r), .S(S[1]));
  Half_Adder half_adder_4 (.A(A[0]), .C(1'b1), .R(half_adder_4_r), .S(S[0]));
endmodule

module MAR (
  input  A,
  input  C,
  input  [3:0] x,
  input  inc,
  output [3:0] y
);

  wire [3:0] function_add1_4bit_1_s, multiplexer_1_out;

  function_add1_4bit function_add1_4bit_1 (.A(y), .S(function_add1_4bit_1_s));
  Registro_MS_4bit registro_ms_4bit_1 (.A(A), .C(C), .x(multiplexer_1_out), .y(y));
  Multiplexer #(.width(4)) multiplexer_1 (.in0(x), .in1(function_add1_4bit_1_s), .out(multiplexer_1_out), .sel(inc));
endmodule

module R_MS_8bit_Z (
  input  A,
  input  C,
  input  [7:0] x,
  input  Z,
  output [7:0] y
);

  wire [7:0] multiplexer_1_out;

  Registro_MS_8bit registro_ms_8bit_1 (.A(A), .C(C), .x(multiplexer_1_out), .y(y));
  Multiplexer #(.width(8)) multiplexer_1 (.in0(x), .in1({8{1'b0}}), .out(multiplexer_1_out), .sel(Z));
endmodule

module boot_counter (
  input  A,
  input  C,
  input  rst_addr,
  output [3:0] y
);

  wire or_1_out;
  wire [3:0] function_add1_4bit_1_s, multiplexer_1_out;

  function_add1_4bit function_add1_4bit_1 (.A(y), .S(function_add1_4bit_1_s));
  Registro_MS_4bit registro_ms_4bit_1 (.A(or_1_out), .C(C), .x(multiplexer_1_out), .y(y));
  or or_1 (or_1_out, A, rst_addr);
  Multiplexer #(.width(4)) multiplexer_1 (
    .in0(function_add1_4bit_1_s), .in1(4'b0000), .out(multiplexer_1_out), .sel(rst_addr));
endmodule

module boot_controller (
  input  start,
  input  C,
  output A_boot,
  output S_ram
);

  wire ff_ms_1_y;

  and and_1 (A_boot, start, ~ff_ms_1_y);  // AND_Gate
  and and_2 (S_ram, start, ff_ms_1_y);
  FF_MS ff_ms_1 (.A(C), .C(C), .F(A_boot), .y(ff_ms_1_y));  // open: not_y
endmodule
